# Fritzing sketch breadboard (saved by Fritzing 0.9.3b)
circuit board: 8.46667cm x 5.64444cm
breadboards: 1

parts:
  C2 = Electrolytic Capacitor [capacitance=1µF package="100 mil [THT, electrolytic]"]
  Photon = Photon
  7805 = Voltage Regulator [package=78xxl]
  C1 = Electrolytic Capacitor [capacitance=10µF voltage=50V package="100 mil [THT, electrolytic]"]

nets:
  GND: C2.-, Photon.GND, 7805.GND, C1.-
  N1: C2.+, Photon.VIN, 7805.OUT
  N2: 7805.IN, C1.+

notes:
  WARNING: up to 18V! This will damage your microcontroller!
